# Fritzing sketch example-write-schematic (saved by Fritzing 0.5.2b)
breadboards: 1

parts:
  Arduino1 = Arduino
  LED1 = Red LED - 5mm [package="5 mm [THT]"]
  R1 = Resistor [resistance=330 package=THT]
  4051 = IC, DIP package, 16 pins [chip_label=IC spacing=300mil]

nets:
  N1: Arduino1.GND, LED1.anode, 4051.pin7, 4051.pin8
  N2: Arduino1.D6, 4051.pin3
  N3: Arduino1.D4, 4051.pin11
  N4: Arduino1.D3, 4051.pin10
  N5: Arduino1.D2, 4051.pin9
  N6: Arduino1.+5V, 4051.pin6, 4051.pin16
  N7: LED1.cathode, R1.Pin_0
  N8: R1.Pin_1, 4051.pin13
